// Logisim project BOTOES.circ as structural Verilog: 1 circuit, main circuit main
module main (
);

  wire _0_out, _1_out, _2_out, _3_out, _4_out, _5_out, _6_out, _7_out, _8_out, _9_out, or_1_out, or_2_out,
       or_3_out, or_4_out, or_5_out, or_6_out, or_7_out, or_8_out, or_9_out, or_10_out, or_11_out, or_12_out,
       or_13_out;

  Button _2 (.out(_2_out));
  Button _1 (.out(_1_out));
  Button _4 (.out(_4_out));
  Button _3 (.out(_3_out));
  Button _5 (.out(_5_out));
  Button _6 (.out(_6_out));
  Button _7 (.out(_7_out));
  Button _8 (.out(_8_out));
  Button _0 (.out(_0_out));
  Button _9 (.out(_9_out));
  or or_1 (or_1_out, _0_out, _9_out);
  or or_2 (or_2_out, _0_out, _9_out, _8_out, _7_out);
  or or_3 (or_3_out, _8_out, _9_out, _2_out);
  or or_4 (or_4_out, or_3_out, _3_out, _4_out, _5_out, _6_out);
  or or_5 (or_5_out, _0_out, _9_out, _8_out, _7_out);
  or or_6 (or_6_out, _0_out, _9_out, _8_out, _7_out, _6_out);
  or or_7 (or_7_out, or_1_out, _8_out, _6_out, _5_out, _4_out);
  or or_8 (or_8_out, or_2_out, _6_out, _5_out, _3_out, _2_out);
  or or_9 (or_9_out, or_5_out, _4_out, _3_out, _2_out, _1_out);
  or or_10 (or_10_out, _0_out, _8_out, _6_out, _2_out);
  or or_11 (or_11_out, _0_out, _8_out);
  or or_12 (or_12_out, or_6_out, _5_out, _4_out, _3_out, _1_out);
  _7_Segment_Display u_7_segment_display_1 (
    .g(or_4_out), .f(or_7_out), .a(or_8_out), .b(or_9_out), .e(or_10_out), .d(or_13_out), .c(or_12_out));  // open: dp
  or or_13 (or_13_out, or_11_out, _6_out, _5_out, _3_out, _2_out);
endmodule
