// Logisim project Contador 7 segmentos Funcionando até o 9.circ as structural Verilog: 9 circuits, main circuit main
module main (
  input  in_1
);

  wire and_1_out, and_2_out, and_3_out, and_4_out, and_5_out, and_6_out, and_7_out, and_8_out, and_9_out,
       and_10_out, and_11_out, and_12_out, and_13_out, and_14_out, and_15_out, and_16_out, clock_1_out,
       j_k_ff_1_q, j_k_ff_1_qn, j_k_ff_2_q, j_k_ff_2_qn, j_k_ff_3_q, j_k_ff_3_qn, j_k_ff_4_q, not_1_out,
       not_2_out, not_3_out, not_4_out, not_5_out, not_6_out, not_7_out, not_8_out, not_9_out, or_1_out,
       or_2_out, or_3_out, or_4_out, or_5_out, or_6_out;

  Clock clock_1 (.out(clock_1_out));
  J_K_Flip_Flop j_k_ff_1 (
    .J(in_1), .clk(clock_1_out), .K(in_1), .Q(j_k_ff_1_q), .Qn(j_k_ff_1_qn), .reset(and_1_out));  // open: preset, en
  J_K_Flip_Flop j_k_ff_2 (
    .J(in_1), .clk(j_k_ff_1_qn), .K(in_1), .Q(j_k_ff_2_q), .Qn(j_k_ff_2_qn), .reset(and_1_out));  // open: preset, en
  and and_1 (and_1_out, j_k_ff_4_q, j_k_ff_2_q);
  J_K_Flip_Flop j_k_ff_3 (
    .J(in_1), .clk(j_k_ff_2_qn), .K(in_1), .Q(j_k_ff_3_q), .Qn(j_k_ff_3_qn), .reset(and_1_out));  // open: preset, en
  not not_1 (not_1_out, j_k_ff_1_q);
  not not_2 (not_2_out, j_k_ff_2_q);
  not not_3 (not_3_out, j_k_ff_4_q);
  not not_4 (not_4_out, j_k_ff_2_q);
  not not_5 (not_5_out, j_k_ff_4_q);
  J_K_Flip_Flop j_k_ff_4 (
    .J(in_1), .clk(j_k_ff_3_qn), .K(in_1), .Q(j_k_ff_4_q), .reset(and_1_out));  // open: Qn, preset, en
  and and_2 (and_2_out, j_k_ff_4_q, not_1_out);
  not not_6 (not_6_out, j_k_ff_3_q);
  and and_3 (and_3_out, not_6_out, not_1_out, not_1_out);
  and and_4 (and_4_out, not_1_out, not_6_out);
  and and_5 (and_5_out, not_2_out, j_k_ff_4_q);
  and and_6 (and_6_out, not_1_out, not_2_out);
  and and_7 (and_7_out, not_2_out, j_k_ff_4_q);
  and and_8 (and_8_out, not_1_out, not_3_out);
  and and_9 (and_9_out, j_k_ff_3_q, not_3_out);
  and and_10 (and_10_out, j_k_ff_2_q, j_k_ff_4_q);
  not not_7 (not_7_out, j_k_ff_2_q);
  and and_11 (and_11_out, not_7_out, not_8_out);
  not not_8 (not_8_out, j_k_ff_3_q);
  and and_12 (and_12_out, j_k_ff_3_q, j_k_ff_4_q);
  and and_13 (and_13_out, not_4_out, j_k_ff_4_q);
  and and_14 (and_14_out, j_k_ff_3_q, j_k_ff_4_q);
  and and_15 (and_15_out, j_k_ff_2_q, not_5_out);
  not not_9 (not_9_out, j_k_ff_2_q);
  and and_16 (and_16_out, not_9_out, not_9_out, j_k_ff_4_q);
  or or_1 (or_1_out, j_k_ff_2_q, and_3_out, and_2_out);
  or or_2 (or_2_out, and_4_out, and_5_out);
  or or_3 (or_3_out, and_6_out, j_k_ff_3_q, and_7_out, and_8_out);
  or or_4 (or_4_out, j_k_ff_1_q, and_9_out, and_10_out, and_11_out);
  or or_5 (or_5_out, and_12_out, and_13_out);
  or or_6 (or_6_out, and_14_out, and_15_out, and_16_out);
  _7_Segment_Display u_7_segment_display_1 (
    .g(or_1_out), .f(or_2_out), .a(or_3_out), .b(or_4_out), .e(or_5_out), .d(or_6_out));  // open: c, dp
endmodule

module Decodificador (
  input  in_1,
  input  in_2,
  input  in_3,
  input  in_4,
  output A,
  output B,
  output C,
  output D,
  output E,
  output F,
  output G
);

  wire and_1_out, and_2_out, and_3_out, and_4_out, and_5_out, and_6_out, and_7_out, and_8_out, and_9_out,
       and_10_out, and_11_out, and_12_out, and_13_out, not_1_out, not_2_out, not_3_out, not_4_out, not_5_out,
       not_6_out, not_7_out, not_8_out, not_9_out, not_10_out, not_11_out, not_12_out, not_13_out,
       not_14_out, not_15_out, not_16_out, not_17_out, not_18_out, or_1_out, xor_1_out;

  not not_1 (not_1_out, in_4);
  not not_2 (not_2_out, in_3);
  not not_3 (not_3_out, in_4);
  not not_4 (not_4_out, in_3);
  not not_5 (not_5_out, in_4);
  not not_6 (not_6_out, in_4);
  not not_7 (not_7_out, in_2);
  not not_8 (not_8_out, in_3);
  not not_9 (not_9_out, in_4);
  not not_10 (not_10_out, in_4);
  not not_11 (not_11_out, in_2);
  xor xor_1 (xor_1_out, in_3, in_2);
  and and_1 (and_1_out, not_1_out, in_3);
  and and_2 (and_2_out, not_2_out, in_2);
  and and_3 (and_3_out, not_3_out, not_4_out);
  and and_4 (and_4_out, not_5_out, in_2);
  and and_5 (and_5_out, in_4, in_2);
  and and_6 (and_6_out, in_4, in_3);
  and and_7 (and_7_out, not_6_out, not_7_out);
  and and_8 (and_8_out, not_8_out, not_9_out);
  and and_9 (and_9_out, in_4, in_3);
  not not_12 (not_12_out, in_4);
  or or_1 (or_1_out, in_3, not_13_out);
  not not_13 (not_13_out, in_2);
  and and_10 (and_10_out, not_10_out, in_3);
  not not_14 (not_14_out, in_4);
  and and_11 (and_11_out, not_14_out, not_11_out);
  and and_12 (and_12_out, in_3, not_15_out);
  not not_15 (not_15_out, in_2);
  not not_16 (not_16_out, in_3);
  and and_13 (and_13_out, in_4, not_16_out, in_2);
  not not_17 (not_17_out, in_2);
  or or_2 (D, in_1, not_17_out, and_8_out, and_9_out);
  and and_14 (E, not_12_out, or_1_out);
  or or_3 (A, xor_1_out, and_1_out, in_1);
  or or_4 (B, in_1, and_2_out, and_3_out, and_4_out);
  or or_5 (C, in_1, and_5_out, and_6_out, and_7_out);
  not not_18 (not_18_out, in_3);
  or or_6 (F, and_10_out, and_11_out, and_12_out, and_13_out);
  or or_7 (G, in_4, not_18_out, in_2, in_1);
endmodule

module \Contador_até_9  (
  output Clock,
  output out_2,
  output out_3,
  output out_4,
  output out_5,
  output out_6,
  output out_7,
  output out_8
);

  wire clock_1_out, j_k_ff_1_q, j_k_ff_1_qn, j_k_ff_2_q, j_k_ff_2_qn, j_k_ff_3_q, j_k_ff_3_qn, j_k_ff_4_q;

  Clock clock_1 (.out(clock_1_out));
  J_K_Flip_Flop j_k_ff_1 (
    .J(1'b1), .clk(clock_1_out), .K(1'b1), .Q(j_k_ff_1_q), .Qn(j_k_ff_1_qn), .reset(Clock));  // open: preset, en
  J_K_Flip_Flop j_k_ff_2 (
    .J(1'b1), .clk(j_k_ff_1_qn), .K(1'b1), .Q(j_k_ff_2_q), .Qn(j_k_ff_2_qn), .reset(Clock));  // open: preset, en
  and and_1 (Clock, j_k_ff_4_q, j_k_ff_2_q);
  J_K_Flip_Flop j_k_ff_3 (
    .J(1'b1), .clk(j_k_ff_2_qn), .K(1'b1), .Q(j_k_ff_3_q), .Qn(j_k_ff_3_qn), .reset(Clock));  // open: preset, en
  Decodificador decodificador_1 (
    .in_1(j_k_ff_4_q), .in_2(j_k_ff_3_q), .in_3(j_k_ff_2_q), .in_4(j_k_ff_1_q), .A(out_2), .B(out_3),
    .C(out_4), .D(out_5), .E(out_6), .F(out_7), .G(out_8));
  J_K_Flip_Flop j_k_ff_4 (
    .J(1'b1), .clk(j_k_ff_3_qn), .K(1'b1), .Q(j_k_ff_4_q), .reset(Clock));  // open: Qn, preset, en
endmodule

module Relogio (
  input  in_1
);

  wire \contador_até_6_1_clock , \contador_até_6_1_out_3 , \contador_até_6_1_out_4 ,
       \contador_até_6_1_out_5 , \contador_até_6_1_out_6 , \contador_até_6_1_out_7 ,
       \contador_até_6_1_out_8 , \contador_até_6_1_out_9 , \contador_até_6_2_clock ,
       \contador_até_6_2_out_3 , \contador_até_6_2_out_4 , \contador_até_6_2_out_5 ,
       \contador_até_6_2_out_6 , \contador_até_6_2_out_7 , \contador_até_6_2_out_8 ,
       \contador_até_6_2_out_9 , \contador_até_9_1_clock , \contador_até_9_1_out_2 ,
       \contador_até_9_1_out_3 , \contador_até_9_1_out_4 , \contador_até_9_1_out_5 ,
       \contador_até_9_1_out_6 , \contador_até_9_1_out_7 , \contador_até_9_1_out_8 ,
       \contador_até_9_minuto_1_clock , \contador_até_9_minuto_1_out_3 , \contador_até_9_minuto_1_out_4 ,
       \contador_até_9_minuto_1_out_5 , \contador_até_9_minuto_1_out_6 , \contador_até_9_minuto_1_out_7 ,
       \contador_até_9_minuto_1_out_8 , \contador_até_9_minuto_1_out_9 , n0_2_horas_1__2_horas,
       n0_2_horas_1_out_4, n0_2_horas_1_out_5, n0_2_horas_1_out_6, n0_2_horas_1_out_7, n0_2_horas_1_out_8,
       n0_2_horas_1_out_9, n0_2_horas_1_out_10, n24hrs_1_clock, n24hrs_1_out_4, n24hrs_1_out_5,
       n24hrs_1_out_6, n24hrs_1_out_7, n24hrs_1_out_8, n24hrs_1_out_9, n24hrs_1_out_10;

  _0_2_horas u_0_2_horas_1 (
    .in_1(n24hrs_1_clock), ._2_horas(n0_2_horas_1__2_horas), .out_4(n0_2_horas_1_out_4),
    .out_5(n0_2_horas_1_out_5), .out_6(n0_2_horas_1_out_6), .out_7(n0_2_horas_1_out_7),
    .out_8(n0_2_horas_1_out_8), .out_9(n0_2_horas_1_out_9), .out_10(n0_2_horas_1_out_10));  // open: Clock
  _24hrs u_24hrs_1 (
    ._24hrs(n0_2_horas_1__2_horas), .in_2(\contador_até_6_1_clock ), .Clock(n24hrs_1_clock),
    .out_4(n24hrs_1_out_4), .out_5(n24hrs_1_out_5), .out_6(n24hrs_1_out_6), .out_7(n24hrs_1_out_7),
    .out_8(n24hrs_1_out_8), .out_9(n24hrs_1_out_9), .out_10(n24hrs_1_out_10));
  \Contador_até_6  \contador_até_6_1  (
    .in_1(\contador_até_9_minuto_1_clock ), .Clock(\contador_até_6_1_clock ),
    .out_3(\contador_até_6_1_out_3 ), .out_4(\contador_até_6_1_out_4 ), .out_5(\contador_até_6_1_out_5 ),
    .out_6(\contador_até_6_1_out_6 ), .out_7(\contador_até_6_1_out_7 ), .out_8(\contador_até_6_1_out_8 ),
    .out_9(\contador_até_6_1_out_9 ));
  \Contador_até_9_minuto  \contador_até_9_minuto_1  (
    .in_1(\contador_até_6_2_clock ), .Clock(\contador_até_9_minuto_1_clock ),
    .out_3(\contador_até_9_minuto_1_out_3 ), .out_4(\contador_até_9_minuto_1_out_4 ),
    .out_5(\contador_até_9_minuto_1_out_5 ), .out_6(\contador_até_9_minuto_1_out_6 ),
    .out_7(\contador_até_9_minuto_1_out_7 ), .out_8(\contador_até_9_minuto_1_out_8 ),
    .out_9(\contador_até_9_minuto_1_out_9 ));
  \Contador_até_6  \contador_até_6_2  (
    .in_1(\contador_até_9_1_clock ), .Clock(\contador_até_6_2_clock ), .out_3(\contador_até_6_2_out_3 ),
    .out_4(\contador_até_6_2_out_4 ), .out_5(\contador_até_6_2_out_5 ), .out_6(\contador_até_6_2_out_6 ),
    .out_7(\contador_até_6_2_out_7 ), .out_8(\contador_até_6_2_out_8 ), .out_9(\contador_até_6_2_out_9 ));
  \Contador_até_9  \contador_até_9_1  (
    .Clock(\contador_até_9_1_clock ), .out_2(\contador_até_9_1_out_2 ), .out_3(\contador_até_9_1_out_3 ),
    .out_4(\contador_até_9_1_out_4 ), .out_5(\contador_até_9_1_out_5 ), .out_6(\contador_até_9_1_out_6 ),
    .out_7(\contador_até_9_1_out_7 ), .out_8(\contador_até_9_1_out_8 ));
  _7_Segment_Display u_7_segment_display_1 (
    .g(n0_2_horas_1_out_4), .f(n0_2_horas_1_out_5), .a(n0_2_horas_1_out_6), .b(n0_2_horas_1_out_7),
    .e(n0_2_horas_1_out_8), .d(n0_2_horas_1_out_9), .c(n0_2_horas_1_out_10));  // open: dp
  _7_Segment_Display u_7_segment_display_2 (
    .g(n24hrs_1_out_4), .f(n24hrs_1_out_5), .a(n24hrs_1_out_6), .b(n24hrs_1_out_7), .e(n24hrs_1_out_8),
    .d(n24hrs_1_out_9), .c(n24hrs_1_out_10));  // open: dp
  _7_Segment_Display u_7_segment_display_3 (
    .g(\contador_até_6_1_out_3 ), .f(\contador_até_6_1_out_4 ), .a(\contador_até_6_1_out_5 ),
    .b(\contador_até_6_1_out_6 ), .e(\contador_até_6_1_out_7 ), .d(\contador_até_6_1_out_8 ),
    .c(\contador_até_6_1_out_9 ));  // open: dp
  _7_Segment_Display u_7_segment_display_4 (
    .g(\contador_até_9_minuto_1_out_3 ), .f(\contador_até_9_minuto_1_out_4 ),
    .a(\contador_até_9_minuto_1_out_5 ), .b(\contador_até_9_minuto_1_out_6 ),
    .e(\contador_até_9_minuto_1_out_7 ), .d(\contador_até_9_minuto_1_out_8 ),
    .c(\contador_até_9_minuto_1_out_9 ), .dp(in_1));
  _7_Segment_Display u_7_segment_display_5 (
    .g(\contador_até_6_2_out_3 ), .f(\contador_até_6_2_out_4 ), .a(\contador_até_6_2_out_5 ),
    .b(\contador_até_6_2_out_6 ), .e(\contador_até_6_2_out_7 ), .d(\contador_até_6_2_out_8 ),
    .c(\contador_até_6_2_out_9 ));  // open: dp
  _7_Segment_Display u_7_segment_display_6 (
    .g(\contador_até_9_1_out_2 ), .f(\contador_até_9_1_out_3 ), .a(\contador_até_9_1_out_4 ),
    .b(\contador_até_9_1_out_5 ), .e(\contador_até_9_1_out_6 ), .d(\contador_até_9_1_out_7 ),
    .c(\contador_até_9_1_out_8 ));  // open: dp
endmodule

module \Contador_até_6  (
  input  in_1,
  output Clock,
  output out_3,
  output out_4,
  output out_5,
  output out_6,
  output out_7,
  output out_8,
  output out_9
);

  wire j_k_ff_1_q, j_k_ff_1_qn, j_k_ff_2_q, j_k_ff_2_qn, j_k_ff_3_q, j_k_ff_3_qn, j_k_ff_4_q;

  J_K_Flip_Flop j_k_ff_1 (
    .J(1'b1), .clk(in_1), .K(1'b1), .Q(j_k_ff_1_q), .Qn(j_k_ff_1_qn), .reset(Clock));  // open: preset, en
  J_K_Flip_Flop j_k_ff_2 (
    .J(1'b1), .clk(j_k_ff_1_qn), .K(1'b1), .Q(j_k_ff_2_q), .Qn(j_k_ff_2_qn), .reset(Clock));  // open: preset, en
  and and_1 (Clock, j_k_ff_3_q, j_k_ff_2_q);
  J_K_Flip_Flop j_k_ff_3 (
    .J(1'b1), .clk(j_k_ff_2_qn), .K(1'b1), .Q(j_k_ff_3_q), .Qn(j_k_ff_3_qn), .reset(Clock));  // open: preset, en
  Decodificador decodificador_1 (
    .in_1(j_k_ff_4_q), .in_2(j_k_ff_3_q), .in_3(j_k_ff_2_q), .in_4(j_k_ff_1_q), .A(out_3), .B(out_4),
    .C(out_5), .D(out_6), .E(out_7), .F(out_8), .G(out_9));
  J_K_Flip_Flop j_k_ff_4 (
    .J(1'b1), .clk(j_k_ff_3_qn), .K(1'b1), .Q(j_k_ff_4_q), .reset(Clock));  // open: Qn, preset, en
endmodule

module \Contador_até_9_minuto  (
  input  in_1,
  output Clock,
  output out_3,
  output out_4,
  output out_5,
  output out_6,
  output out_7,
  output out_8,
  output out_9
);

  wire j_k_ff_1_q, j_k_ff_1_qn, j_k_ff_2_q, j_k_ff_2_qn, j_k_ff_3_q, j_k_ff_3_qn, j_k_ff_4_q;

  J_K_Flip_Flop j_k_ff_1 (
    .J(1'b1), .clk(in_1), .K(1'b1), .Q(j_k_ff_1_q), .Qn(j_k_ff_1_qn), .reset(Clock));  // open: preset, en
  J_K_Flip_Flop j_k_ff_2 (
    .J(1'b1), .clk(j_k_ff_1_qn), .K(1'b1), .Q(j_k_ff_2_q), .Qn(j_k_ff_2_qn), .reset(Clock));  // open: preset, en
  and and_1 (Clock, j_k_ff_4_q, j_k_ff_2_q);
  J_K_Flip_Flop j_k_ff_3 (
    .J(1'b1), .clk(j_k_ff_2_qn), .K(1'b1), .Q(j_k_ff_3_q), .Qn(j_k_ff_3_qn), .reset(Clock));  // open: preset, en
  Decodificador decodificador_1 (
    .in_1(j_k_ff_4_q), .in_2(j_k_ff_3_q), .in_3(j_k_ff_2_q), .in_4(j_k_ff_1_q), .A(out_3), .B(out_4),
    .C(out_5), .D(out_6), .E(out_7), .F(out_8), .G(out_9));
  J_K_Flip_Flop j_k_ff_4 (
    .J(1'b1), .clk(j_k_ff_3_qn), .K(1'b1), .Q(j_k_ff_4_q), .reset(Clock));  // open: Qn, preset, en
endmodule

module _24hrs (
  input  _24hrs,
  input  in_2,
  output Clock,
  output out_4,
  output out_5,
  output out_6,
  output out_7,
  output out_8,
  output out_9,
  output out_10
);

  wire and_1_out, and_2_out, j_k_ff_1_q, j_k_ff_1_qn, j_k_ff_2_q, j_k_ff_2_qn, j_k_ff_3_q, j_k_ff_3_qn,
       j_k_ff_4_q, not_1_out, not_2_out, or_1_out;

  or or_1 (or_1_out, and_2_out, and_1_out);
  J_K_Flip_Flop j_k_ff_1 (
    .J(1'b1), .clk(in_2), .K(1'b1), .Q(j_k_ff_1_q), .Qn(j_k_ff_1_qn), .reset(or_1_out));  // open: preset, en
  J_K_Flip_Flop j_k_ff_2 (
    .J(1'b1), .clk(j_k_ff_1_qn), .K(1'b1), .Q(j_k_ff_2_q), .Qn(j_k_ff_2_qn), .reset(or_1_out));  // open: preset, en
  and and_1 (and_1_out, j_k_ff_4_q, j_k_ff_2_q);
  J_K_Flip_Flop j_k_ff_3 (
    .J(1'b1), .clk(j_k_ff_2_qn), .K(1'b1), .Q(j_k_ff_3_q), .Qn(j_k_ff_3_qn), .reset(or_1_out));  // open: preset, en
  Decodificador decodificador_1 (
    .in_1(j_k_ff_4_q), .in_2(j_k_ff_3_q), .in_3(j_k_ff_2_q), .in_4(j_k_ff_1_q), .A(out_4), .B(out_5),
    .C(out_6), .D(out_7), .E(out_8), .F(out_9), .G(out_10));
  or or_2 (Clock, and_2_out, and_1_out);
  J_K_Flip_Flop j_k_ff_4 (
    .J(1'b1), .clk(j_k_ff_3_qn), .K(1'b1), .Q(j_k_ff_4_q), .reset(or_1_out));  // open: Qn, preset, en
  not not_1 (not_1_out, j_k_ff_1_q);
  not not_2 (not_2_out, j_k_ff_2_q);
  and and_2 (and_2_out, not_1_out, _24hrs, not_2_out, j_k_ff_3_q);
endmodule

module _0_2_horas (
  input  in_1,
  output Clock,
  output _2_horas,
  output out_4,
  output out_5,
  output out_6,
  output out_7,
  output out_8,
  output out_9,
  output out_10
);

  wire j_k_ff_1_q, j_k_ff_1_qn, j_k_ff_2_q, j_k_ff_2_qn, j_k_ff_3_q, j_k_ff_3_qn, j_k_ff_4_q, not_1_out;

  J_K_Flip_Flop j_k_ff_1 (
    .J(1'b1), .clk(in_1), .K(1'b1), .Q(j_k_ff_1_q), .Qn(j_k_ff_1_qn), .reset(Clock));  // open: preset, en
  J_K_Flip_Flop j_k_ff_2 (
    .J(1'b1), .clk(j_k_ff_1_qn), .K(1'b1), .Q(j_k_ff_2_q), .Qn(j_k_ff_2_qn), .reset(Clock));  // open: preset, en
  and and_1 (Clock, j_k_ff_1_q, j_k_ff_2_q);
  not not_1 (not_1_out, j_k_ff_1_q);
  and and_2 (_2_horas, not_1_out, j_k_ff_2_q);
  J_K_Flip_Flop j_k_ff_3 (
    .J(1'b1), .clk(j_k_ff_2_qn), .K(1'b1), .Q(j_k_ff_3_q), .Qn(j_k_ff_3_qn), .reset(Clock));  // open: preset, en
  Decodificador decodificador_1 (
    .in_1(j_k_ff_4_q), .in_2(j_k_ff_3_q), .in_3(j_k_ff_2_q), .in_4(j_k_ff_1_q), .A(out_4), .B(out_5),
    .C(out_6), .D(out_7), .E(out_8), .F(out_9), .G(out_10));
  J_K_Flip_Flop j_k_ff_4 (
    .J(1'b1), .clk(j_k_ff_3_qn), .K(1'b1), .Q(j_k_ff_4_q), .reset(Clock));  // open: Qn, preset, en
endmodule

module Contador_9____0 (
  input  in_1
);

  wire and_1_out, and_2_out, and_3_out, and_4_out, and_5_out, and_6_out, and_7_out, and_8_out, and_9_out,
       and_10_out, and_11_out, and_12_out, and_13_out, and_14_out, and_15_out, and_16_out, clock_1_out,
       j_k_ff_1_q, j_k_ff_2_q, j_k_ff_3_q, j_k_ff_3_qn, j_k_ff_4_q, j_k_ff_4_qn, not_1_out, not_2_out,
       not_3_out, not_4_out, not_5_out, not_6_out, not_7_out, not_8_out, not_9_out, not_10_out, not_11_out,
       not_12_out, not_13_out, not_14_out, not_15_out, not_16_out, not_17_out, not_18_out, or_1_out,
       or_2_out, or_3_out, or_4_out, or_5_out, or_6_out, or_7_out, xor_1_out;

  J_K_Flip_Flop j_k_ff_1 (.J(in_1), .K(in_1), .Q(j_k_ff_1_q), .reset(and_1_out));  // open: clk, Qn, preset, en
  J_K_Flip_Flop j_k_ff_2 (.J(in_1), .K(in_1), .Q(j_k_ff_2_q), .reset(and_1_out));  // open: clk, Qn, preset, en
  and and_1 (and_1_out, j_k_ff_4_q, j_k_ff_2_q);
  J_K_Flip_Flop j_k_ff_3 (
    .J(in_1), .clk(and_2_out), .K(in_1), .Q(j_k_ff_3_q), .Qn(j_k_ff_3_qn), .reset(and_1_out));  // open: preset, en
  and and_2 (and_2_out, clock_1_out, j_k_ff_4_qn);
  not not_1 (not_1_out, j_k_ff_1_q);
  not not_2 (not_2_out, j_k_ff_2_q);
  not not_3 (not_3_out, j_k_ff_1_q);
  not not_4 (not_4_out, j_k_ff_2_q);
  not not_5 (not_5_out, j_k_ff_1_q);
  not not_6 (not_6_out, j_k_ff_1_q);
  not not_7 (not_7_out, j_k_ff_3_q);
  not not_8 (not_8_out, j_k_ff_2_q);
  not not_9 (not_9_out, j_k_ff_1_q);
  not not_10 (not_10_out, j_k_ff_1_q);
  not not_11 (not_11_out, j_k_ff_3_q);
  J_K_Flip_Flop j_k_ff_4 (
    .J(in_1), .clk(clock_1_out), .K(in_1), .Q(j_k_ff_4_q), .Qn(j_k_ff_4_qn), .reset(and_1_out));  // open: preset, en
  xor xor_1 (xor_1_out, j_k_ff_2_q, j_k_ff_3_q);
  and and_3 (and_3_out, not_1_out, j_k_ff_2_q);
  and and_4 (and_4_out, not_2_out, j_k_ff_3_q);
  and and_5 (and_5_out, not_3_out, not_4_out);
  and and_6 (and_6_out, not_5_out, j_k_ff_3_q);
  and and_7 (and_7_out, j_k_ff_1_q, j_k_ff_3_q);
  and and_8 (and_8_out, j_k_ff_1_q, j_k_ff_2_q);
  and and_9 (and_9_out, not_6_out, not_7_out);
  and and_10 (and_10_out, not_8_out, not_9_out);
  and and_11 (and_11_out, j_k_ff_1_q, j_k_ff_2_q);
  not not_12 (not_12_out, j_k_ff_1_q);
  or or_1 (or_1_out, j_k_ff_2_q, not_13_out);
  not not_13 (not_13_out, j_k_ff_3_q);
  and and_12 (and_12_out, not_10_out, j_k_ff_2_q);
  not not_14 (not_14_out, j_k_ff_1_q);
  and and_13 (and_13_out, not_14_out, not_11_out);
  and and_14 (and_14_out, j_k_ff_2_q, not_15_out);
  not not_15 (not_15_out, j_k_ff_3_q);
  not not_16 (not_16_out, j_k_ff_2_q);
  and and_15 (and_15_out, j_k_ff_1_q, not_16_out, j_k_ff_3_q);
  or or_2 (or_2_out, j_k_ff_4_q, not_17_out, and_10_out, and_11_out);
  not not_17 (not_17_out, j_k_ff_3_q);
  and and_16 (and_16_out, not_12_out, or_1_out);
  Clock clock_1 (.out(clock_1_out));
  or or_3 (or_3_out, xor_1_out, and_3_out, j_k_ff_4_q);
  or or_4 (or_4_out, j_k_ff_4_q, and_4_out, and_5_out, and_6_out);
  or or_5 (or_5_out, j_k_ff_4_q, and_7_out, and_8_out, and_9_out, and_9_out);
  not not_18 (not_18_out, j_k_ff_2_q);
  or or_6 (or_6_out, and_12_out, and_13_out, and_14_out, and_15_out);
  or or_7 (or_7_out, j_k_ff_1_q, not_18_out, j_k_ff_3_q, j_k_ff_4_q);
  _7_Segment_Display u_7_segment_display_1 (
    .g(or_3_out), .f(or_4_out), .a(or_5_out), .b(or_2_out), .e(and_16_out), .d(or_6_out), .c(or_7_out));  // open: dp
endmodule
