// Logisim project logisim - Teclado trabalho.circ as structural Verilog
module main (
  input  in_1,
  input  in_2,
  output [6:0] out_3
);

  wire aA_out, bB_out, button_1_out, button_2_out, clock_1_out, Limpa_Tela_out, s_r_ff_1_q;

  Button Limpa_Tela (.out(Limpa_Tela_out));
  Button aA (.out(aA_out));
  Button bB (.out(bB_out));
  teclado teclado_1 (.\Saída (bB_out), .A(aA_out), .B(bB_out), .Caps_Lock(s_r_ff_1_q), .\Binário (out_3));
  Clock clock_1 (.out(clock_1_out));
  Button button_1 (.out(button_1_out));
  TTY tty_1 (.data(out_3), .clk(clock_1_out), .we(in_2), .clr(Limpa_Tela_out));
  Button button_2 (.out(button_2_out));
  S_R_Flip_Flop s_r_ff_1 (
    .clk(in_1), .Q(s_r_ff_1_q), .preset(button_1_out), .reset(button_2_out));  // open: S, R, Qn, en
  LED led_1 (.in(s_r_ff_1_q));
endmodule

module A (
  input  a,
  input  A_2,
  output [6:0] \Binário 
);

  or or_1 (\Binário [6], A_2, a);

  assign \Binário [5:0] = {a, 4'b0000, \Binário [6]};
endmodule

module B (
  input  b,
  input  B_2,
  output [6:0] \Binário 
);

  or or_1 (\Binário [6], B_2, b);

  assign \Binário [5:0] = {b, 3'b000, \Binário [6], 1'b0};
endmodule

module teclado (
  input  A,
  input  B,
  input  Caps_Lock,
  input  \Saída ,
  output [6:0] \Binário 
);

  wire demultiplexer_1_out0, demultiplexer_1_out1, demultiplexer_2_out0, demultiplexer_2_out1;
  wire [6:0] \Codificador_A_binário , \Codificador_B_binário ;

  Demultiplexer demultiplexer_1 (
    .out0(demultiplexer_1_out0), .out1(demultiplexer_1_out1), .in(A), .sel(Caps_Lock));  // open: en
  A Codificador_A (.a(demultiplexer_1_out0), .A_2(demultiplexer_1_out1), .\Binário (\Codificador_A_binário ));
  Multiplexer #(.width(7)) multiplexer_1 (
    .in0(\Codificador_A_binário ), .in1(\Codificador_B_binário ), .out(\Binário ), .sel(\Saída ));  // open: en
  Demultiplexer demultiplexer_2 (
    .out0(demultiplexer_2_out0), .out1(demultiplexer_2_out1), .in(B), .sel(Caps_Lock));  // open: en
  B Codificador_B (.b(demultiplexer_2_out0), .B_2(demultiplexer_2_out1), .\Binário (\Codificador_B_binário ));
endmodule

module C (
  input  c,
  input  C_2,
  output [6:0] out_3
);

  or or_1 (out_3[6], C_2, c);

  assign out_3[5:0] = {c, 3'b000, {2{out_3[6]}}};
endmodule
