// Logisim project logisin.circ as structural Verilog: 1 circuit, main circuit main
module main (
  input  A2,
  input  A1,
  input  A0,
  input  B2,
  input  B1,
  input  B0,
  output Bit_0,
  output Bit_1,
  output Bit_2,
  output Carry_out
);

  wire and_1_out, and_2_out, and_3_out, and_4_out, and_5_out, and_6_out, and_7_out, or_1_out, xor_2_out,
       xor_3_out;

  xor xor_1 (Bit_0, B0, A0);
  and and_1 (and_1_out, B0, A0);
  xor xor_2 (xor_2_out, B1, A1);
  xor xor_3 (xor_3_out, B2, A2);
  and and_2 (and_2_out, B1, A1);
  and and_3 (and_3_out, B1, and_1_out);
  and and_4 (and_4_out, A1, and_1_out);
  and and_5 (and_5_out, B2, A2);
  and and_6 (and_6_out, or_1_out, B2);
  and and_7 (and_7_out, A2, or_1_out);
  xor xor_4 (Bit_1, xor_2_out, and_1_out);
  xor xor_5 (Bit_2, or_1_out, xor_3_out);
  or or_1 (or_1_out, and_2_out, and_3_out, and_4_out);
  or or_2 (Carry_out, and_5_out, and_6_out, and_7_out);

  // Notes on the sheet:
  //   Carry out 1
  //   Carry out 2
endmodule
